# Fritzing sketch MEARM (saved by Fritzing 0.9.3b)
breadboards: 1

parts:
  Part1 = Arduino Uno (Rev3)
  R2 = Rotary Potentiometer (Small) [maximum_resistance=100kΩ package=THT]
  R3 = Rotary Potentiometer (Small) [maximum_resistance=100kΩ package=THT]
  R4 = Rotary Potentiometer (Small) [maximum_resistance=100kΩ package=THT]
  R5 = Rotary Potentiometer (Small) [maximum_resistance=100kΩ package=THT]
  M4 = Dagu DGServo 9g (End View) [part_number=RS001B]
  M5 = Dagu DGServo 9g (End View) [part_number=RS001B]
  M6 = Dagu DGServo 9g (End View) [part_number=RS001B]
  M7 = Dagu DGServo 9g (End View) [part_number=RS001B]

nets:
  N1: Part1.A0, R2.wiper
  N2: Part1.A1, R3.wiper
  N3: Part1.A2, R4.wiper
  N4: Part1.A3, R5.wiper
  N5: Part1.D9_PWM, M5.pulse
  N6: Part1.D10_PWM/SS, M6.pulse
  N7: Part1.D11_PWM/MOSI, M7.pulse
  N8: Part1.D5_PWM, M4.pulse
  VCC: Part1.5V, R2.leg2, R3.leg2, R4.leg2, R5.leg2, M4.vcc, M5.vcc, M6.vcc, M7.vcc
  GND: Part1.GND, R2.leg1, R3.leg1, R4.leg1, R5.leg1, M4.gnd, M5.gnd, M6.gnd, M7.gnd

// code stored in the sketch: mearm.ino
//zoomkat dual pot/servo test 12-29-12
//view output using the serial monitor

#include <Servo.h> 
Servo myservo1;
Servo myservo2;
Servo myservo3;
Servo myservo4;

int potpin1 = 0;  //my pot pin
int potpin2 = 1;
int potpin3 = 2;
int potpin4 = 3;

int newval1, oldval1;
int newval2, oldval2;
int newval3, oldval3;
int newval4, oldval4;

void setup() 
{
  Serial.begin(9600);  
  myservo1.attach(5);  
  myservo2.attach(9);
  myservo3.attach(10);
  myservo4.attach(11);
  Serial.println("testing dual pot servo");  
}

void loop()
{ 
  newval1 = analogRead(potpin1);           
  newval1 = map(newval1, 0, 1023, 0, 179); 
  if (newval1 < (oldval1-2) || newval1 > (oldval1+2)){  
    myservo1.write(newval1);
    Serial.print("1- ");
    Serial.println(newval1);
    oldval1=newval1;
  }

  newval2 = analogRead(potpin2);
  newval2 = map(newval2, 0, 1023, 0, 179);
  if (newval2 < (oldval2-2) || newval2 > (oldval2+2)){  
    myservo2.write(newval2);
    Serial.print("2- ");    
    Serial.println(newval2);
    oldval2=newval2;
  }
  delay(50);
  {
  }
  
  newval3 = analogRead(potpin3);           
  newval3 = map(newval3, 0, 1023, 0, 179); 
  if (newval1 < (oldval1-2) || newval3 > (oldval3+2)){  
    myservo1.write(newval3);
    Serial.print("3- ");
    Serial.println(newval3);
    oldval3=newval3;
  }
  {
  } 
  newval4 = analogRead(potpin4);           
  newval4 = map(newval4, 0, 1023, 0, 179); 
  if (newval1 < (oldval1-2) || newval4 > (oldval4+2)){  
    myservo1.write(newval4);
    Serial.print("4- ");
    Serial.println(newval4);
    oldval4=newval4;

  } 
  }
